# Fritzing sketch air_quality_monitor (saved by Fritzing 0.9.4)

parts:
  U1 = ESP32-38PinWide [part_number=ESP32-38PinWide]
  Componente1 = Adafruit_BMP280
  Componente2 = Adafruit CCS811
  Componente3 = Adafruit CCS811
  Part2 = KY-015 Temperature & Humidity Sensor Module [package="Breakout board"]

nets:
  3.3V: U1.3.3, U1.EN, U1.GPIO36, Componente1.3.3V, Componente2.3.3V, Componente3.VIN, Componente3.3.3V
  VIN: U1.VIN, Part2.Vin
  N1: U1.GPIO2, U1.GPIO0, U1.GPIO4, Part2.S
  GND: U1.GPIO18, U1.GPIO19, U1.GND, U1.GPIO23, Componente1.GND, Componente2.GND, Componente3.GND, Part2.-
  N2: U1.GPIO21, Componente1.SDO/ADR, Componente2.SDA, Componente3.SDA
  N3: U1.GPIO3, U1.GPIO1, U1.GPIO22, Componente1.SCK/SCL, Componente2.SCL, Componente3.SCL

custom parts:
  ESP32-38PinWide: Generic 38-Pin ESP32 with wide format (only access to one side of pins on a breadboard) based on Stephen Lilley's HiLetgo ESP-WROOM-32 ESP32 ESP-32S Development Board.
  Adafruit_BMP280: Bosch has stepped up their game with their new BMP280 sensor, an environmental sensor with temperature, barometric pressure that is the next generation upgrade to the BMP085/BMP180/BMP183. This sensor is great for all sorts of weather sensing and can even be used in both I2C and SPI! This precision sensor from Bosch is the best low-cost, precision sensing solution for measuring barometric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
  KY-015 Temperature & Humidity Sensor Module: KY-015 temperature and humidity sensor module, provides a low-latency serial interface to measure humidity and temperature.
